// Logisim project branch_comp.circ as structural Verilog: 1 circuit, main circuit branch_comp
module branch_comp (
  input  [31:0] rs1,
  input  [31:0] rs2,
  input  BrUn,
  output BrEq,
  output BrLt
);

  wire eq1, eq2, lt1, lt2;

  Comparator #(.width(32)) comparator_1 (.a(rs1), .b(rs2), .eq(eq1), .lt(lt1));  // open: gt
  Comparator #(.mode("unsigned"), .width(32)) comparator_2 (.a(rs1), .b(rs2), .eq(eq2), .lt(lt2));  // open: gt
  Multiplexer multiplexer_1 (.in0(eq1), .in1(eq2), .out(BrEq), .sel(BrUn));
  Multiplexer multiplexer_2 (.in0(lt1), .in1(lt2), .out(BrLt), .sel(BrUn));

  // Notes on the sheet:
  //   INPUTS to your circuit
  //   DON'T CHANGE THE LOCATIONS OF THE INPUTS AND OUTPUTS!
  //   OUTPUT from your circuit
endmodule
