// Logisim project control_logic.circ as structural Verilog: 1 circuit, main circuit control_logic
module control_logic (
  input  [31:0] inst,
  input  BrEq,
  input  BrLt,
  output PCSel,
  output RegWEn,
  output [2:0] ImmSel,
  output BrUn,
  output ASel,
  output BSel,
  output [3:0] ALUSel,
  output MemRW,
  output [1:0] WBSel,
  output CSRSel,
  output CSRWen
);

  wire and_1_out, demultiplexer_1_out0, demultiplexer_1_out4, demultiplexer_1_out5, demultiplexer_1_out13,
       demultiplexer_1_out25, demultiplexer_1_out28, I, I1, I2, multiplexer_10_out, not_1_out, not_3_out,
       PCSelSB, R, SB, U, UJ, WBSelI;
  wire [2:0] multiplexer_11_out, multiplexer_12_out, multiplexer_13_out, multiplexer_14_out;
  wire [3:0] ALUSelI, ALUSelR, ALUSelU, multiplexer_2_out, multiplexer_3_out, multiplexer_4_out,
       multiplexer_5_out, multiplexer_6_out, multiplexer_8_out, multiplexer_15_out, multiplexer_16_out;

  not not_1 (not_1_out, inst[4]);
  and and_1 (and_1_out, inst[6], not_1_out);
  Multiplexer multiplexer_1 (.in0(and_1_out), .in1(PCSelSB), .out(PCSel), .sel(SB));
  or or_1 (RegWEn, R, U, UJ, I);
  Demultiplexer #(.select(5)) demultiplexer_1 (
    .out0(demultiplexer_1_out0), .out4(demultiplexer_1_out4), .out5(demultiplexer_1_out5), .out8(MemRW),
    .out12(R), .out13(demultiplexer_1_out13), .out24(SB), .out25(demultiplexer_1_out25), .out27(UJ),
    .out28(demultiplexer_1_out28), .in(1'b1), .sel(inst[6:2]));  // open: out1, out2, out3, out6, out7, out9, out10, out11, out14, out15, out16, out17, out18, out19, out20, out21, out22, out23, out26, out29, out30, out31
  or or_2 (I1, demultiplexer_1_out0, demultiplexer_1_out4);
  or or_3 (ASel, U, UJ, SB);
  or or_4 (I2, demultiplexer_1_out25, demultiplexer_1_out28);
  not not_2 (BSel, R);
  or or_5 (U, demultiplexer_1_out5, demultiplexer_1_out13);
  or or_6 (I, I1, I2);
  and and_2 (WBSel[1], inst[6], inst[2]);
  and and_3 (WBSel[0], I, WBSelI);
  Multiplexer #(.select(2), .width(4)) multiplexer_2 (
    .in0(4'b0000), .in1(4'b1100), .in2(4'b1010), .out(multiplexer_2_out), .sel({inst[25], inst[30]}));  // open: in3
  Multiplexer #(.width(4)) multiplexer_3 (.in0(4'b0110), .in1(4'b1110), .out(multiplexer_3_out), .sel(inst[25]));
  Multiplexer #(.width(4)) multiplexer_4 (.in0(4'b0000), .in1(ALUSelU), .out(multiplexer_4_out), .sel(U));
  Multiplexer #(.width(4)) multiplexer_5 (.in0(4'b0100), .in1(4'b0101), .out(multiplexer_5_out), .sel(inst[30]));
  Multiplexer #(.width(4)) multiplexer_6 (.in0(4'b0000), .in1(ALUSelR), .out(multiplexer_6_out), .sel(R));
  assign ALUSel = multiplexer_4_out | multiplexer_6_out | multiplexer_8_out;  // OR_Gate or_7, 4 bits wide
  Multiplexer #(.select(3), .width(4)) multiplexer_7 (
    .in0(multiplexer_2_out), .in1(multiplexer_3_out), .in2(4'b0111), .in3(4'b1011), .in4(4'b0011),
    .in5(multiplexer_5_out), .in6(4'b0010), .in7(4'b0001), .out(ALUSelR), .sel(inst[14:12]));
  Multiplexer #(.width(4)) multiplexer_8 (.in0(4'b0000), .in1(ALUSelI), .out(multiplexer_8_out), .sel(I));
  Multiplexer multiplexer_9 (.in0(multiplexer_10_out), .in1(not_3_out), .out(PCSelSB), .sel(inst[12]));
  not not_3 (not_3_out, multiplexer_10_out);
  Multiplexer multiplexer_10 (.in0(BrEq), .in1(BrLt), .out(multiplexer_10_out), .sel(inst[14]));
  Multiplexer #(.width(3)) multiplexer_11 (.in0(3'b000), .in1(3'b001), .out(multiplexer_11_out), .sel(MemRW));
  Multiplexer #(.width(3)) multiplexer_12 (.in0(3'b000), .in1(3'b010), .out(multiplexer_12_out), .sel(SB));
  assign ImmSel = multiplexer_11_out | multiplexer_12_out | multiplexer_13_out | multiplexer_14_out;  // OR_Gate or_8, 3 bits wide
  Multiplexer #(.width(3)) multiplexer_13 (.in0(3'b000), .in1(3'b011), .out(multiplexer_13_out), .sel(U));
  Multiplexer #(.width(3)) multiplexer_14 (.in0(3'b000), .in1(3'b100), .out(multiplexer_14_out), .sel(UJ));
  not not_4 (WBSelI, inst[4]);
  Multiplexer #(.width(4)) multiplexer_15 (.in0(4'b0100), .in1(4'b0101), .out(multiplexer_15_out), .sel(inst[30]));
  Multiplexer #(.select(3), .width(4)) multiplexer_16 (
    .in0(4'b0000), .in1(4'b0110), .in2(4'b0111), .in4(4'b0011), .in5(multiplexer_15_out), .in6(4'b0010),
    .in7(4'b0001), .out(multiplexer_16_out), .sel(inst[14:12]));  // open: in3
  Multiplexer #(.width(4)) multiplexer_17 (.in0(4'b0000), .in1(multiplexer_16_out), .out(ALUSelI), .sel(inst[4]));
  Multiplexer #(.width(4)) multiplexer_18 (.in0(4'b0000), .in1(4'b1101), .out(ALUSelU), .sel(inst[5]));

  assign BrUn = inst[13];

  // Other names for the same wires on the sheet: funct7[6:0] = inst[31:25]; opcode0[4:0] = inst[6:2]; f0 = inst[12];
  //   funct3[2:0] = inst[14:12]; f1 = inst[13]; f2 = inst[14]; S = MemRW

  // Notes on the sheet:
  //   INPUTS to your circuit
  //   Get instruction-type
  //   UJ-type operations
  //   OUTPUT from your circuit
  //   R-type operations
  //   S-type operations
  //   SB-type operations
  //   I-type operations
  //   U-type operations
endmodule
