// Logisim project imm_gen.circ as structural Verilog: 1 circuit, main circuit imm_gen
module imm_gen (
  input  [31:0] inst,
  input  [2:0] ImmSel,
  output [31:0] imm
);

  wire [31:0] I, S, SB, UB;

  assign I = {{20{inst[31]}}, inst[31:20]};  // Bit_Extender bit_extender_1
  assign S = {{20{inst[31]}}, {inst[31:25], inst[11:7]}};  // Bit_Extender bit_extender_2
  Multiplexer #(.select(3), .width(32)) multiplexer_1 (
    .in0(I), .in1(S), .in2(SB), .in3({inst[31:12], {12{1'b0}}}), .in4(UB), .out(imm), .sel(ImmSel));  // open: in5, in6, in7
  assign SB = {{19{inst[31]}}, {inst[31], inst[7], inst[30:25], inst[11:8], 1'b0}};  // Bit_Extender bit_extender_3
  assign UB = {{11{inst[31]}}, {inst[31], inst[19:12], inst[20], inst[30:21], 1'b0}};  // Bit_Extender bit_extender_4

  // Other names for the same wires on the sheet: in811[3:0] = inst[11:8]; in7 = inst[7]; in2124[3:0] = inst[24:21];
  //   U[31:12] = inst[31:12]; in2530[5:0] = inst[30:25]; in20 = inst[20]; in1219[7:0] = inst[19:12]; in31 = inst[31]

  // Notes on the sheet:
  //   INPUTS to your circuit
  //   Split relevant bits
  //   Select instruction type
  //   Generate Imm-value for each type
  //   OUTPUT from your circuit
endmodule
