// Logisim project regfile.circ as structural Verilog: 1 circuit, main circuit regfile
module regfile (
  input  [4:0] rs1,
  input  [4:0] rs2,
  input  [4:0] rd,
  input  [31:0] Write_Data,
  input  RegWEn,
  input  clk,
  output [31:0] ra,
  output [31:0] sp,
  output [31:0] t0,
  output [31:0] t1,
  output [31:0] t2,
  output [31:0] s0,
  output [31:0] s1,
  output [31:0] a0,
  output [31:0] Read_Data_1,
  output [31:0] Read_Data_2
);

  wire w0, w1, w2, w3, w4, w5, w6, w7, w8, w9, w10, w11, w12, w13, w14, w15, w16, w17, w18, w19, w20, w21,
       w22, w23, w24, w25, w26, w27, w28, w29, w30, w31;
  wire [31:0] r0, r3, r4, r11, r12, r13, r14, r15, r16, r17, r18, r19, r20, r21, r22, r23, r24, r25, r26,
       r27, r28, r29, r30, r31;

  Register #(.width(32)) register_1 (.D(Write_Data), .en(w16), .clk(clk), .Q(r16));  // open: clr
  Register #(.width(32)) register_2 (.D(Write_Data), .en(w20), .clk(clk), .Q(r20));  // open: clr
  Demultiplexer #(.select(5)) demultiplexer_1 (
    .out0(w0), .out1(w1), .out2(w2), .out3(w3), .out4(w4), .out5(w5), .out6(w6), .out7(w7), .out8(w8),
    .out9(w9), .out10(w10), .out11(w11), .out12(w12), .out13(w13), .out14(w14), .out15(w15), .out16(w16),
    .out17(w17), .out18(w18), .out19(w19), .out20(w20), .out21(w21), .out22(w22), .out23(w23), .out24(w24),
    .out25(w25), .out26(w26), .out27(w27), .out28(w28), .out29(w29), .out30(w30), .out31(w31), .in(RegWEn),
    .sel(rd));
  Register #(.width(32)) register_3 (.D(Write_Data), .en(w17), .clk(clk), .Q(r17));  // open: clr
  Register #(.width(32)) register_4 (.D(Write_Data), .en(w21), .clk(clk), .Q(r21));  // open: clr
  Register #(.width(32)) register_5 (.D(Write_Data), .en(1'b0), .clk(clk), .Q(r0));  // open: clr
  Register #(.width(32)) register_6 (.D(Write_Data), .en(w4), .clk(clk), .Q(r4));  // open: clr
  Register #(.width(32)) register_7 (.D(Write_Data), .en(w8), .clk(clk), .Q(s0));  // open: clr
  Register #(.width(32)) register_8 (.D(Write_Data), .en(w18), .clk(clk), .Q(r18));  // open: clr
  Register #(.width(32)) register_9 (.D(Write_Data), .en(w22), .clk(clk), .Q(r22));  // open: clr
  Register #(.width(32)) register_10 (.D(Write_Data), .en(w12), .clk(clk), .Q(r12));  // open: clr
  Register #(.width(32)) register_11 (.D(Write_Data), .en(w1), .clk(clk), .Q(ra));  // open: clr
  Register #(.width(32)) register_12 (.D(Write_Data), .en(w5), .clk(clk), .Q(t0));  // open: clr
  Register #(.width(32)) register_13 (.D(Write_Data), .en(w9), .clk(clk), .Q(s1));  // open: clr
  Register #(.width(32)) register_14 (.D(Write_Data), .en(w13), .clk(clk), .Q(r13));  // open: clr
  Register #(.width(32)) register_15 (.D(Write_Data), .en(w19), .clk(clk), .Q(r19));  // open: clr
  Register #(.width(32)) register_16 (.D(Write_Data), .en(w23), .clk(clk), .Q(r23));  // open: clr
  Register #(.width(32)) register_17 (.D(Write_Data), .en(w2), .clk(clk), .Q(sp));  // open: clr
  Register #(.width(32)) register_18 (.D(Write_Data), .en(w6), .clk(clk), .Q(t1));  // open: clr
  Register #(.width(32)) register_19 (.D(Write_Data), .en(w10), .clk(clk), .Q(a0));  // open: clr
  Multiplexer #(.select(5), .width(32)) multiplexer_1 (
    .in0(r0), .in1(ra), .in2(sp), .in3(r3), .in4(r4), .in5(t0), .in6(t1), .in7(t2), .in8(s0), .in9(s1),
    .in10(a0), .in11(r11), .in12(r12), .in13(r13), .in14(r14), .in15(r15), .in16(r16), .in17(r17),
    .in18(r18), .in19(r19), .in20(r20), .in21(r21), .in22(r22), .in23(r23), .in24(r24), .in25(r25),
    .in26(r26), .in27(r27), .in28(r28), .in29(r29), .in30(r30), .in31(r31), .out(Read_Data_1), .sel(rs1));
  Register #(.width(32)) register_20 (.D(Write_Data), .en(w14), .clk(clk), .Q(r14));  // open: clr
  Register #(.width(32)) register_21 (.D(Write_Data), .en(w24), .clk(clk), .Q(r24));  // open: clr
  Register #(.width(32)) register_22 (.D(Write_Data), .en(w28), .clk(clk), .Q(r28));  // open: clr
  Register #(.width(32)) register_23 (.D(Write_Data), .en(w3), .clk(clk), .Q(r3));  // open: clr
  Register #(.width(32)) register_24 (.D(Write_Data), .en(w7), .clk(clk), .Q(t2));  // open: clr
  Register #(.width(32)) register_25 (.D(Write_Data), .en(w11), .clk(clk), .Q(r11));  // open: clr
  Register #(.width(32)) register_26 (.D(Write_Data), .en(w15), .clk(clk), .Q(r15));  // open: clr
  Register #(.width(32)) register_27 (.D(Write_Data), .en(w25), .clk(clk), .Q(r25));  // open: clr
  Register #(.width(32)) register_28 (.D(Write_Data), .en(w29), .clk(clk), .Q(r29));  // open: clr
  Register #(.width(32)) register_29 (.D(Write_Data), .en(w26), .clk(clk), .Q(r26));  // open: clr
  Register #(.width(32)) register_30 (.D(Write_Data), .en(w30), .clk(clk), .Q(r30));  // open: clr
  Multiplexer #(.select(5), .width(32)) multiplexer_2 (
    .in0(r0), .in1(ra), .in2(sp), .in3(r3), .in4(r4), .in5(t0), .in6(t1), .in7(t2), .in8(s0), .in9(s1),
    .in10(a0), .in11(r11), .in12(r12), .in13(r13), .in14(r14), .in15(r15), .in16(r16), .in17(r17),
    .in18(r18), .in19(r19), .in20(r20), .in21(r21), .in22(r22), .in23(r23), .in24(r24), .in25(r25),
    .in26(r26), .in27(r27), .in28(r28), .in29(r29), .in30(r30), .in31(r31), .out(Read_Data_2), .sel(rs2));
  Register #(.width(32)) register_31 (.D(Write_Data), .en(w27), .clk(clk), .Q(r27));  // open: clr
  Register #(.width(32)) register_32 (.D(Write_Data), .en(w31), .clk(clk), .Q(r31));  // open: clr

  // Other names for the same wires on the sheet: r1[31:0] = ra; r2[31:0] = sp; r5[31:0] = t0; r6[31:0] = t1;
  //   r7[31:0] = t2; r8[31:0] = s0; r9[31:0] = s1; r10[31:0] = a0; read_data1[31:0] = Read_Data_1;
  //   read_data2[31:0] = Read_Data_2; read_reg1[4:0] = rs1; read_reg2[4:0] = rs2; write_en = RegWEn;
  //   write_reg[4:0] = rd

  // Notes on the sheet:
  //   INPUTS to your circuit
  //   demux write_en to register
  //   These are DEBUG/TEST outputs from your circuit.
  //   Registers
  //   mux values from rs1 and rs2
  //   OUTPUTS from your circuit
endmodule
